# Fritzing sketch Nano (saved by Fritzing 0.9.3b)
circuit board: 6.94872cm x 4.67468cm
breadboards: 1

parts:
  Nano1 = Arduino Nano v2.3
  J1 = female pin header, 2 pins [form="♀ (female)"]
  J2 = female pin header, 2 pins [form="♀ (female)"]
  J3 = female pin header, 2 pins [form="♀ (female)"]
  J4 = female pin header, 2 pins [form="♀ (female)"]
  J5 = female pin header, 2 pins [form="♀ (female)"]
  J6 = female pin header, 2 pins [form="♀ (female)"]
  J7 = female pin header, 2 pins [form="♀ (female)"]
  J8 = female pin header, 2 pins [form="♀ (female)"]
  J9 = female pin header, 2 pins [form="♀ (female)"]
  J10 = female pin header, 2 pins [form="♀ (female)"]
  J11 = female pin header, 2 pins [form="♀ (female)"]
  J12 = female pin header, 2 pins [form="♀ (female)"]
  J13 = female pin header, 2 pins [form="♀ (female)"]
  J14 = female pin header, 2 pins [form="♀ (female)"]
  J15 = female pin header, 2 pins [form="♀ (female)"]
  J16 = female pin header, 2 pins [form="♀ (female)"]
  J17 = female pin header, 2 pins [form="♀ (female)"]
  J18 = female pin header, 2 pins [form="♀ (female)"]
  J19 = female pin header, 2 pins [form="♀ (female)"]
  J20 = female pin header, 2 pins [form="♀ (female)"]

nets:
  N1: Nano1.D1TX, J9.pin1
  N2: Nano1.D0RX, J9.pin2
  N3: Nano1.RST, J2.pin1, J10.pin1
  N4: Nano1.GND, J1.pin2, J10.pin2, J17.pin1, J17.pin2, J18.pin1, J18.pin2, J19.pin1, J19.pin2, J20.pin1, J20.pin2
  N5: Nano1.D2, J12.pin1
  N6: Nano1.D3, J12.pin2
  N7: Nano1.D4, J11.pin1
  N8: Nano1.D5, J11.pin2
  N9: Nano1.D6, J16.pin1
  N10: Nano1.D7, J16.pin2
  N11: Nano1.D8, J15.pin1
  N12: Nano1.D9, J15.pin2
  N13: Nano1.D10, J13.pin1
  N14: Nano1.D11, J13.pin2
  N15: Nano1.D12, J14.pin1
  N16: Nano1.D13, J7.pin1
  N17: Nano1.3V3, J8.pin2
  N18: Nano1.AREF, J8.pin1
  N19: Nano1.A7, J5.pin2
  N20: Nano1.A6, J5.pin1
  N21: Nano1.A5, J6.pin2
  N22: Nano1.A4, J6.pin1
  N23: Nano1.A3, J3.pin2
  N24: Nano1.A2, J3.pin1
  N25: Nano1.A1, J4.pin2
  N26: Nano1.A0, J4.pin1
  N27: Nano1.+5V, J2.pin2
  N28: Nano1.VIN, J1.pin1

notes:
  vin
  gnd
  rst
  +5V
  A0
  A7
  3V3
  D13
  TX
  RX
  D2
  D12
