# Fritzing sketch Placa Encoders (saved by Fritzing 0.9.2b)
circuit board: 3.2106cm x 1.86915cm
breadboards: 1

parts:
  J1 = female pin header, 2 pins [form="♀ (female)"]
  J2 = female pin header, 2 pins [form="♀ (female)"]
  J3 = female pin header, 2 pins [form="♀ (female)"]
  J4 = female pin header, 2 pins [form="♀ (female)"]
  J5 = female pin header, 2 pins [form="♀ (female)"]
  J6 = female pin header, 2 pins [form="♀ (female)"]
  J7 = female pin header, 2 pins [form="♀ (female)"]

nets:
  N1: J1.pin1, J3.pin1, J5.pin1
  N2: J1.pin2, J3.pin2, J5.pin2
  N3: J2.pin1, J6.pin1
  N4: J2.pin2, J6.pin2
  N5: J4.pin1, J7.pin1
  N6: J4.pin2, J7.pin2

notes:
  GND - VCC - A - B
