# Fritzing sketch PlacaSD (saved by Fritzing 0.9.3b)
circuit board: 8.62068cm x 4.04832cm
breadboards: 1

parts:
  R1 = Resistor [tolerance=±5% resistance=100 package=THT]
  R2 = Resistor [tolerance=±5% resistance=100 package=THT]
  R3 = Resistor [tolerance=±5% resistance=100 package=THT]
  R4 = Resistor [tolerance=±5% resistance=100 package=THT]
  R5 = Resistor [tolerance=±5% resistance=100 package=THT]
  R6 = Resistor [tolerance=±5% resistance=100 package=THT]
  R7 = Resistor [tolerance=±5% resistance=100 package=THT]
  R8 = Resistor [tolerance=±5% resistance=100 package=THT]
  R9 = Resistor [tolerance=±5% resistance=100 package=THT]
  JP1 = Header 2 [package=molex-1x2_lock]
  JP2 = Header 2 [package=molex-1x2_lock]
  JP3 = Header 2 [package=molex-1x2_lock]
  JP4 = Header 2 [package=molex-1x2_lock]
  JP5 = Header 2 [package=molex-1x2_lock]
  JP6 = Header 2 [package=molex-1x2_lock]

nets:
  N1: R1.Pin_0, JP2.2
  N2: R1.Pin_1, R2.Pin_0, JP5.1
  N3: R2.Pin_1, R3.Pin_0
  N4: R3.Pin_1, R6.Pin_1, R9.Pin_1, JP1.1, JP4.2
  N5: R4.Pin_0, JP2.1
  N6: R4.Pin_1, R5.Pin_0, JP5.2
  N7: R5.Pin_1, R6.Pin_0
  N8: R7.Pin_0, JP3.2
  N9: R7.Pin_1, R8.Pin_0, JP6.1
  N10: R8.Pin_1, R9.Pin_0
  N11: JP1.2, JP4.1
  N12: JP3.1, JP6.2

notes:
  Entradas (Pinos Arduino Mega)
  Saidas (Pinos Módulo SD)
  Vcc 5V
  GND
  CS
  MISO
  SCK
  MOSI
  51
  52
  53
  50
