# Fritzing sketch ArduinoMega (saved by Fritzing 0.9.3b)
circuit board: 11.0726cm x 8.65504cm
breadboards: 1

parts:
  Componente2 = Arduino Mega ADK (Rev3)
  Driver = female pin header, 3 pins [form="♀ (female)"]
  Driver_2 = female pin header, 3 pins [form="♀ (female)"]
  Encoder = female pin header, 2 pins [form="♀ (female)"]
  Encoder1 = female pin header, 2 pins [form="♀ (female)"]
  GPS = female pin header, 2 pins [form="♀ (female)"]
  GPS_2 = female pin header, 2 pins [form="♀ (female)"]
  IMU = female pin header, 2 pins [form="♀ (female)"]
  SD = female pin header, 2 pins [form="♀ (female)"]
  RC = female pin header, 3 pins [form="♀ (female)"]
  botao = female pin header, 2 pins [form="♀ (female)"]
  SD1 = female pin header, 2 pins [form="♀ (female)"]
  US = female pin header, 2 pins [form="♀ (female)"]
  US2 = female pin header, 2 pins [form="♀ (female)"]
  US4 = female pin header, 2 pins [form="♀ (female)"]
  US8 = female pin header, 2 pins [form="♀ (female)"]
  US9 = female pin header, 2 pins [form="♀ (female)"]
  US12 = female pin header, 2 pins [form="♀ (female)"]
  US13 = female pin header, 2 pins [form="♀ (female)"]
  US15 = female pin header, 2 pins [form="♀ (female)"]
  PWM = female pin header, 2 pins [form="♀ (female)"]
  PWM_2 = female pin header, 2 pins [form="♀ (female)"]
  RXTX = female pin header, 2 pins [form="♀ (female)"]
  VinGnd = female pin header, 2 pins [form="♀ (female)"]
  5V = female pin header, 2 pins [form="♀ (female)"]
  Gnd3V = female pin header, 2 pins [form="♀ (female)"]
  GnDReset = female pin header, 2 pins [form="♀ (female)"]
  Gnd3V_2 = female pin header, 2 pins [form="♀ (female)"]
  GndReset = female pin header, 2 pins [form="♀ (female)"]
  Gnd5V = female pin header, 2 pins [form="♀ (female)"]
  5V3 = female pin header, 2 pins [form="♀ (female)"]
  5V4 = female pin header, 2 pins [form="♀ (female)"]
  A = female pin header, 2 pins [form="♀ (female)"]
  A_2 = female pin header, 2 pins [form="♀ (female)"]
  A_3 = female pin header, 2 pins [form="♀ (female)"]
  A_4 = female pin header, 2 pins [form="♀ (female)"]
  botao2 = female pin header, 2 pins [form="♀ (female)"]
  A_5 = female pin header, 3 pins [form="♀ (female)"]
  Gnd = female pin header, 2 pins [form="♀ (female)"]
  Gnd_2 = female pin header, 2 pins [form="♀ (female)"]
  US_2 = female pin header, 2 pins [form="♀ (female)"]
  US16 = female pin header, 2 pins [form="♀ (female)"]
  US17 = female pin header, 2 pins [form="♀ (female)"]
  US18 = female pin header, 2 pins [form="♀ (female)"]
  US19 = female pin header, 2 pins [form="♀ (female)"]
  Gnd_3 = female pin header, 2 pins [form="♀ (female)"]
  GND = female pin header, 2 pins [form="♀ (female)"]
  5V_2 = female pin header, 2 pins [form="♀ (female)"]
  5V_3 = female pin header, 2 pins [form="♀ (female)"]
  US5 = female pin header, 2 pins [form="♀ (female)"]

nets:
  N1: Componente2.A8, A_2.pin1
  N2: Componente2.A9, A_3.pin2
  N3: Componente2.A10, A_3.pin1
  N4: Componente2.A11, A_4.pin2
  N5: Componente2.A12, A_4.pin1
  N6: Componente2.A13, A_5.pin3
  N7: Componente2.A14, A_5.pin2
  N8: Componente2.A15, A_5.pin1
  N9: Componente2.A0, RC.pin3
  N10: Componente2.A1, RC.pin2
  N11: Componente2.A2, RC.pin1
  N12: Componente2.A3, botao.pin1
  N13: Componente2.A4, botao2.pin1
  N14: Componente2.A5, A.pin2
  N15: Componente2.A6, A.pin1
  N16: Componente2.A7, A_2.pin2
  N17: Componente2.D21/SCL, IMU.pin1
  N18: Componente2.D20/SDA, IMU.pin2
  N19: Componente2.D19/RX1, Encoder1.pin1
  N20: Componente2.D18/TX1, Encoder1.pin2
  N21: Componente2.D17/RX2, GPS.pin1
  N22: Componente2.D16/TX2, GPS.pin2
  N23: Componente2.D15/RX3, GPS_2.pin1
  N24: Componente2.D14/TX3, GPS_2.pin2
  N25: Componente2.GND, VinGnd.pin2, 5V.pin1, Gnd3V.pin1, GnDReset.pin1, Gnd3V_2.pin1, GndReset.pin1, Gnd5V.pin1, 5V3.pin1, 5V4.pin1, Gnd.pin1, Gnd.pin2, Gnd_2.pin1, Gnd_2.pin2, Gnd_3.pin1, Gnd_3.pin2, GND.pin1, GND.pin2
  N26: Componente2.D13_PWM, Driver.pin3
  N27: Componente2.D12_PWM, Driver.pin2
  N28: Componente2.D11_PWM, Driver.pin1
  N29: Componente2.D10_PWM, Driver_2.pin3
  N30: Componente2.D9_PWM, Driver_2.pin2
  N31: Componente2.D8_PWM, Driver_2.pin1
  N32: Componente2.RESET, GnDReset.pin2, GndReset.pin2
  N33: Componente2.3V3, Gnd3V.pin2, Gnd3V_2.pin2
  N34: Componente2.5V, botao.pin2, 5V.pin2, Gnd5V.pin2, 5V3.pin2, 5V4.pin2, botao2.pin2, 5V_2.pin1, 5V_2.pin2, 5V_3.pin1, 5V_3.pin2
  N35: Componente2.VIN, VinGnd.pin1
  N36: Componente2.D0/RX0, RXTX.pin1
  N37: Componente2.D1/TX0, RXTX.pin2
  N38: Componente2.D2_PWM, Encoder.pin1
  N39: Componente2.D3_PWM, Encoder.pin2
  N40: Componente2.D4_PWM, PWM.pin1
  N41: Componente2.D5_PWM, PWM.pin2
  N42: Componente2.D6_PWM, PWM_2.pin1
  N43: Componente2.D7_PWM, PWM_2.pin2
  N44: Componente2.D22, US12.pin2
  N45: Componente2.D23, US8.pin2
  N46: Componente2.D24, US12.pin1
  N47: Componente2.D25, US8.pin1
  N48: Componente2.D26, US13.pin2
  N49: Componente2.D27, US9.pin2
  N50: Componente2.D28, US13.pin1
  N51: Componente2.D29, US9.pin1
  N52: Componente2.D30, US19.pin1
  N53: Componente2.D31, US15.pin2
  N54: Componente2.D32, US19.pin2
  N55: Componente2.D33, US15.pin1
  N56: Componente2.D34, US_2.pin1
  N57: Componente2.D35, US5.pin2
  N58: Componente2.D36, US_2.pin2
  N59: Componente2.D37, US5.pin1
  N60: Componente2.D38, US16.pin1
  N61: Componente2.D39, US4.pin2
  N62: Componente2.D40, US16.pin2
  N63: Componente2.D41, US4.pin1
  N64: Componente2.D42, US17.pin2
  N65: Componente2.D43, US2.pin2
  N66: Componente2.D44, US17.pin1
  N67: Componente2.D45, US2.pin1
  N68: Componente2.D46, US18.pin2
  N69: Componente2.D47, US.pin2
  N70: Componente2.D48, US18.pin1
  N71: Componente2.D49, US.pin1
  N72: Componente2.D50/MISO, SD1.pin1
  N73: Componente2.D51/MOSI, SD.pin2
  N74: Componente2.D52/SCK, SD1.pin2
  N75: Componente2.D53/SS, SD.pin1
