# Fritzing sketch TriggerEcho (saved by Fritzing 0.9.3b)
circuit board: 9.5557cm x 8.35856cm
breadboards: 1

parts:
  U1 = SN74LS32N [package="DIP14 [THT]"]
  U2 = SN74LS32N [package="DIP14 [THT]"]
  J1 = female pin header, 2 pins [form="♀ (female)"]
  J2 = female pin header, 2 pins [form="♀ (female)"]
  J3 = female pin header, 2 pins [form="♀ (female)"]
  J4 = female pin header, 2 pins [form="♀ (female)"]
  J5 = female pin header, 2 pins [form="♀ (female)"]
  J6 = female pin header, 2 pins [form="♀ (female)"]
  J7 = female pin header, 2 pins [form="♀ (female)"]
  J8 = female pin header, 2 pins [form="♀ (female)"]
  J10 = female pin header, 2 pins [form="♀ (female)"]
  J11 = female pin header, 2 pins [form="♀ (female)"]
  J12 = female pin header, 2 pins [form="♀ (female)"]
  U3 = SN74LS32N [package="DIP14 [THT]"]
  J13 = female pin header, 2 pins [form="♀ (female)"]
  IC2 = IC, DIP package, 16 pins [chip_label="IC 4051"]
  IC3 = IC, DIP package, 16 pins [chip_label="IC 4051"]
  J16 = female pin header, 2 pins [form="♀ (female)"]
  J17 = female pin header, 3 pins [form="♀ (female)"]
  J18 = female pin header, 3 pins [form="♀ (female)"]
  J19 = female pin header, 2 pins [form="♀ (female)"]

nets:
  N1: U1.1A, J1.pin1
  N2: U1.1B, J2.pin1
  N3: U1.1Y, U1.2A
  N4: U1.2B, J3.pin1
  N5: U1.2Y, U1.3A
  GND: U1.GND, U2.GND, U3.GND, IC2.pin6, IC2.pin7, IC2.pin8, IC3.pin6, IC3.pin7, IC3.pin8, J19.pin2
  N6: U1.3Y, U1.4A
  N7: U1.3B, J4.pin1
  N8: U1.4Y, U2.4B
  N9: U1.4B, J5.pin1
  VCC: U1.Vcc, U2.Vcc, U3.Vcc, IC2.pin16, IC3.pin16, J19.pin1
  N10: U2.1A, J10.pin1
  N11: U2.1B, U2.2Y
  N12: U2.1Y, U3.4B
  N13: U2.2A, J11.pin1
  N14: U2.2B, U2.3Y
  N15: U2.3A, J12.pin1
  N16: U2.3B, U2.4Y
  N17: U2.4A, J6.pin1
  N18: J1.pin2, IC3.pin14
  N19: J2.pin2, IC3.pin13
  N20: J3.pin2, IC3.pin12
  N21: J4.pin2, IC3.pin15
  N22: J5.pin2, IC3.pin5
  N23: J6.pin2, IC2.pin12
  N24: J7.pin1, U3.3A
  N25: J7.pin2, IC2.pin2
  N26: J8.pin1, U3.4A
  N27: J8.pin2, IC2.pin1
  N28: J10.pin2, IC2.pin15
  N29: J11.pin2, IC2.pin14
  N30: J12.pin2, IC2.pin13
  N31: U3.3Y, J13.pin1
  N32: U3.3B, U3.4Y
  N33: IC2.pin3, IC3.pin1
  N34: IC2.pin9, J18.pin1
  N35: IC2.pin10, J18.pin2
  N36: IC2.pin11, J18.pin3
  N37: IC3.pin3, J16.pin2
  N38: IC3.pin9, J17.pin1
  N39: IC3.pin10, J17.pin2
  N40: IC3.pin11, J17.pin3

notes:
  saida echo
  entrada trigger
  us4
  us1
  us2
  us3
  us5
  us6
  us7
  us8
  us9
  us10
  us11
  c1
  c2
  vcc
  gnd
