# Fritzing sketch TriggerEchoMuxDemux (saved by Fritzing 0.9.3b)
circuit board: 11.3025cm x 8.04347cm
breadboards: 1

parts:
  IC3 = IC, DIP package, 16 pins [chip_label="IC 4051"]
  IC5 = IC, DIP package, 16 pins [chip_label="IC 4051"]
  IC4 = IC, DIP package, 16 pins [chip_label="IC 4051"]
  J1 = female pin header, 2 pins [form="♀ (female)"]
  J2 = female pin header, 2 pins [form="♀ (female)"]
  J3 = female pin header, 2 pins [form="♀ (female)"]
  J4 = female pin header, 2 pins [form="♀ (female)"]
  J5 = female pin header, 2 pins [form="♀ (female)"]
  J6 = female pin header, 2 pins [form="♀ (female)"]
  J7 = female pin header, 2 pins [form="♀ (female)"]
  J8 = female pin header, 2 pins [form="♀ (female)"]
  J9 = female pin header, 2 pins [form="♀ (female)"]
  J10 = female pin header, 2 pins [form="♀ (female)"]
  J11 = female pin header, 2 pins [form="♀ (female)"]
  J12 = female pin header, 2 pins [form="♀ (female)"]
  J13 = female pin header, 2 pins [form="♀ (female)"]
  J14 = female pin header, 2 pins [form="♀ (female)"]
  J15 = female pin header, 2 pins [form="♀ (female)"]
  J16 = female alternating pin header, 3 pins [form="♀ (female)"]
  J17 = female pin header, 3 pins [form="♀ (female)"]
  J19 = female pin header, 3 pins [form="♀ (female)"]
  J20 = female pin header, 3 pins [form="♀ (female)"]
  J24 = female pin header, 2 pins [form="♀ (female)"]
  J25 = female pin header, 2 pins [form="♀ (female)"]
  J27 = female pin header, 2 pins [form="♀ (female)"]
  J31 = female pin header, 2 pins [form="♀ (female)"]
  J32 = female pin header, 2 pins [form="♀ (female)"]
  J33 = female pin header, 2 pins [form="♀ (female)"]
  J34 = female pin header, 2 pins [form="♀ (female)"]
  J37 = female pin header, 2 pins [form="♀ (female)"]
  J39 = female pin header, 2 pins [form="♀ (female)"]
  IC2 = IC, DIP package, 16 pins [chip_label="IC 4051"]
  J48 = female pin header, 2 pins [form="♀ (female)"]
  J49 = female pin header, 2 pins [form="♀ (female)"]
  J50 = female pin header, 2 pins [form="♀ (female)"]
  J51 = female pin header, 2 pins [form="♀ (female)"]
  J52 = female pin header, 2 pins [form="♀ (female)"]
  J53 = female pin header, 2 pins [form="♀ (female)"]
  J54 = female pin header, 2 pins [form="♀ (female)"]
  J55 = female pin header, 2 pins [form="♀ (female)"]

nets:
  N1: IC3.pin1, IC2.pin3
  N2: IC3.pin2, J9.pin2
  N3: IC3.pin3, J55.pin1
  N4: IC3.pin4, J1.pin2
  N5: IC3.pin5, J11.pin2
  N6: IC3.pin6, IC3.pin7, IC3.pin8, IC5.pin6, IC5.pin7, IC5.pin8, IC4.pin6, IC4.pin7, IC4.pin8, J24.pin2, J25.pin2, J27.pin2, J31.pin2, J32.pin2, J33.pin2, J34.pin2, J37.pin2, J39.pin2, IC2.pin6, IC2.pin7, IC2.pin8, J48.pin2, J49.pin2, J50.pin2, J51.pin2, J52.pin2, J53.pin2, J54.pin2
  N7: IC3.pin9, J16.pin3
  N8: IC3.pin10, J16.pin2
  N9: IC3.pin11, J16.pin1
  N10: IC3.pin12, J10.pin2
  N11: IC3.pin13, J12.pin2
  N12: IC3.pin14, J2.pin2
  N13: IC3.pin15, J15.pin2
  N14: IC3.pin16, IC5.pin16, IC4.pin16, J24.pin1, J25.pin1, J27.pin1, J31.pin1, J32.pin1, J33.pin1, J34.pin1, J37.pin1, J39.pin1, IC2.pin16, J48.pin1, J49.pin1, J50.pin1, J51.pin1, J52.pin1, J53.pin1, J54.pin1
  N15: IC5.pin1, J6.pin2
  N16: IC5.pin2, J7.pin2
  N17: IC5.pin3, IC4.pin1
  N18: IC5.pin4, J5.pin2
  N19: IC5.pin5, J14.pin2
  N20: IC5.pin9, J20.pin1
  N21: IC5.pin10, J20.pin2
  N22: IC5.pin11, J20.pin3
  N23: IC5.pin12, J3.pin2
  N24: IC5.pin13, J13.pin2
  N25: IC5.pin14, J4.pin2
  N26: IC5.pin15, J8.pin2
  N27: IC4.pin2, J15.pin1
  N28: IC4.pin3, J55.pin2
  N29: IC4.pin4, J2.pin1
  N30: IC4.pin5, J12.pin1
  N31: IC4.pin9, J19.pin3
  N32: IC4.pin10, J19.pin2
  N33: IC4.pin11, J19.pin1
  N34: IC4.pin12, J10.pin1
  N35: IC4.pin13, J11.pin1
  N36: IC4.pin14, J1.pin1
  N37: IC4.pin15, J9.pin1
  N38: J3.pin1, IC2.pin5
  N39: J4.pin1, IC2.pin2
  N40: J5.pin1, IC2.pin13
  N41: J6.pin1, IC2.pin15
  N42: J7.pin1, IC2.pin14
  N43: J8.pin1, IC2.pin1
  N44: J13.pin1, IC2.pin4
  N45: J14.pin1, IC2.pin12
  N46: J17.pin1, IC2.pin9
  N47: J17.pin2, IC2.pin10
  N48: J17.pin3, IC2.pin11

notes:
  v+
  v-
  2
  1
  0
  3
  y0
  4
  6
  7
  5
  Z
  us1
  us2
  us3
  us4
  us5
  us6
  us7
  us8
  us9
  us13
  us14
  us12
  us11
  us15
  us10
  T
  E
  AT
  AE
  vcc
  gnd
